// Logisim project alu.circ as structural Verilog: 14 circuits, main circuit main
module main (
  input  [31:0] X,
  input  [31:0] Y,
  input  [3:0] Switch,
  output Signed_Overflow,
  output Equal,
  output [31:0] Result
);

  wire add_cout, sub_cout;
  wire [31:0] add_sum, addu_sum, and_output, demultiplexer_1_out0, demultiplexer_1_out1,
       demultiplexer_1_out2, demultiplexer_1_out5, demultiplexer_1_out6, demultiplexer_1_out7,
       demultiplexer_1_out8, demultiplexer_1_out9, demultiplexer_1_out10, demultiplexer_1_out14,
       demultiplexer_1_out15, demultiplexer_2_out0, demultiplexer_2_out1, demultiplexer_2_out2,
       demultiplexer_2_out5, demultiplexer_2_out6, demultiplexer_2_out7, demultiplexer_2_out8,
       demultiplexer_2_out9, demultiplexer_2_out10, demultiplexer_2_out14, demultiplexer_2_out15, or_output,
       sll_out, slt_out, sltu_out, sra_out, srl_out, sub_result, subu_result;

  Demultiplexer #(.select(4), .width(32)) demultiplexer_1 (
    .out0(demultiplexer_1_out0), .out1(demultiplexer_1_out1), .out2(demultiplexer_1_out2),
    .out5(demultiplexer_1_out5), .out6(demultiplexer_1_out6), .out7(demultiplexer_1_out7),
    .out8(demultiplexer_1_out8), .out9(demultiplexer_1_out9), .out10(demultiplexer_1_out10),
    .out14(demultiplexer_1_out14), .out15(demultiplexer_1_out15), .in(X), .sel(Switch));  // open: out3, out4, out11, out12, out13, en
  Demultiplexer #(.select(4), .width(32)) demultiplexer_2 (
    .out0(demultiplexer_2_out0), .out1(demultiplexer_2_out1), .out2(demultiplexer_2_out2),
    .out5(demultiplexer_2_out5), .out6(demultiplexer_2_out6), .out7(demultiplexer_2_out7),
    .out8(demultiplexer_2_out8), .out9(demultiplexer_2_out9), .out10(demultiplexer_2_out10),
    .out14(demultiplexer_2_out14), .out15(demultiplexer_2_out15), .in(Y), .sel(Switch));  // open: out3, out4, out11, out12, out13, en
  Equal equal_1 (.X(Y), .Y(X), .Output(Equal));
  \or  \or  (.X(demultiplexer_1_out10), .Y(demultiplexer_2_out10), .Output(or_output));
  sll sll (.B(demultiplexer_1_out0), .A(demultiplexer_2_out0), .out(sll_out));
  srl srl (.B(demultiplexer_1_out1), .A(demultiplexer_2_out1), .out(srl_out));
  sra sra (.B(demultiplexer_1_out2), .A(demultiplexer_2_out2), .out(sra_out));
  add add (.X(demultiplexer_1_out5), .Y(demultiplexer_2_out5), .sum(add_sum), .cout(add_cout));
  addu addu (.X(demultiplexer_1_out6), .Y(demultiplexer_2_out6), .sum(addu_sum));
  sub sub (.in_1(demultiplexer_1_out7), .in_2(demultiplexer_2_out7), .result(sub_result), .cout(sub_cout));
  subu subu (.in_1(demultiplexer_1_out8), .in_2(demultiplexer_2_out8), .result(subu_result));
  \and  \and  (.X(demultiplexer_1_out9), .Y(demultiplexer_2_out9), .Output(and_output));
  slt__signed_comparison slt (.X(demultiplexer_1_out14), .Y(demultiplexer_2_out14), .out(slt_out));
  sltu__unsigned_comparison sltu (.X(demultiplexer_1_out15), .Y(demultiplexer_2_out15), .out(sltu_out));
  Multiplexer #(.select(4), .width(32)) multiplexer_1 (
    .in0(sll_out), .in1(srl_out), .in2(sra_out), .in5(add_sum), .in6(addu_sum), .in7(sub_result),
    .in8(subu_result), .in9(and_output), .in10(or_output), .in14(slt_out), .in15(sltu_out), .out(Result),
    .sel(Switch));  // open: in3, in4, in11, in12, in13, en
  Multiplexer #(.select(4)) multiplexer_2 (
    .in0(1'b0), .in1(1'b0), .in2(1'b0), .in5(add_cout), .in6(1'b0), .in7(sub_cout), .in8(1'b0), .in9(1'b0),
    .in10(1'b0), .in14(1'b0), .in15(1'b0), .out(Signed_Overflow), .sel(Switch));  // open: in3, in4, in11, in12, in13, en

  // Other names for the same wires on the sheet: overflow = Signed_Overflow; S[3:0] = Switch

  // Notes on the sheet:
  //   INPUTS to your circuit
  //   DON'T CHANGE THE LOCATIONS OF THE INPUTS AND OUTPUTS!
  //   OUTPUTS from your circuit
endmodule

module switch (
  input  [31:0] X,
  input  [31:0] Y,
  input  [3:0] Switch,
  output [31:0] out,
  output [31:0] out_2,
  output [31:0] out_3
);

  Demultiplexer #(.select(4), .width(32)) demultiplexer_1 (
    .out0(out), .out2(out_2), .in(X), .sel(Switch));  // open: out1, out3, out4, out5, out6, out7, out8, out9, out10, out11, out12, out13, out14, out15, en
  Demultiplexer #(.select(4), .width(32)) demultiplexer_2 (
    .out0(out_3), .in(Y), .sel(Switch));  // open: out1, out2, out3, out4, out5, out6, out7, out8, out9, out10, out11, out12, out13, out14, out15, en
endmodule

module Equal (
  input  [31:0] X,
  input  [31:0] Y,
  output Output
);

  Comparator #(.width(32), .mode("unsigned")) comparator_1 (.a(X), .b(Y), .eq(Output));  // open: gt, lt
endmodule

module sll (
  input  [31:0] B,
  input  [31:0] A,
  output [31:0] out
);

  wire [31:0] multiplexer_1_out, multiplexer_2_out, multiplexer_3_out, multiplexer_4_out, shifter_1_out,
       shifter_2_out, shifter_3_out, shifter_4_out, shifter_5_out;

  Multiplexer #(.width(32)) multiplexer_1 (
    .in0(B), .in1(shifter_1_out), .out(multiplexer_1_out), .sel(A[0]));  // open: en
  Shifter #(.width(32)) shifter_1 (.in(B), .\dist (5'b00001), .out(shifter_1_out));
  Shifter #(.width(32)) shifter_2 (.in(multiplexer_1_out), .\dist (5'b00010), .out(shifter_2_out));
  Multiplexer #(.width(32)) multiplexer_2 (
    .in0(multiplexer_1_out), .in1(shifter_2_out), .out(multiplexer_2_out), .sel(A[1]));  // open: en
  Shifter #(.width(32)) shifter_3 (.in(multiplexer_2_out), .\dist (5'b00100), .out(shifter_3_out));
  Multiplexer #(.width(32)) multiplexer_3 (
    .in0(multiplexer_2_out), .in1(shifter_3_out), .out(multiplexer_3_out), .sel(A[2]));  // open: en
  Shifter #(.width(32)) shifter_4 (.in(multiplexer_3_out), .\dist (5'b01000), .out(shifter_4_out));
  Multiplexer #(.width(32)) multiplexer_4 (
    .in0(multiplexer_3_out), .in1(shifter_4_out), .out(multiplexer_4_out), .sel(A[3]));  // open: en
  Shifter #(.width(32)) shifter_5 (.in(multiplexer_4_out), .\dist (5'b10000), .out(shifter_5_out));
  Multiplexer #(.width(32)) multiplexer_5 (
    .in0(multiplexer_4_out), .in1(shifter_5_out), .out(out), .sel(A[4]));  // open: en
endmodule

module srl (
  input  [31:0] B,
  input  [31:0] A,
  output [31:0] out
);

  wire [31:0] multiplexer_1_out, multiplexer_2_out, multiplexer_3_out, multiplexer_4_out, shifter_1_out,
       shifter_2_out, shifter_3_out, shifter_4_out, shifter_5_out;

  Multiplexer #(.width(32)) multiplexer_1 (
    .in0(B), .in1(shifter_1_out), .out(multiplexer_1_out), .sel(A[0]));  // open: en
  Shifter #(.width(32), .shift("lr")) shifter_1 (.in(B), .\dist (5'b00001), .out(shifter_1_out));
  Shifter #(.width(32), .shift("lr")) shifter_2 (.in(multiplexer_1_out), .\dist (5'b00010), .out(shifter_2_out));
  Multiplexer #(.width(32)) multiplexer_2 (
    .in0(multiplexer_1_out), .in1(shifter_2_out), .out(multiplexer_2_out), .sel(A[1]));  // open: en
  Shifter #(.width(32), .shift("lr")) shifter_3 (.in(multiplexer_2_out), .\dist (5'b00100), .out(shifter_3_out));
  Multiplexer #(.width(32)) multiplexer_3 (
    .in0(multiplexer_2_out), .in1(shifter_3_out), .out(multiplexer_3_out), .sel(A[2]));  // open: en
  Shifter #(.width(32), .shift("lr")) shifter_4 (.in(multiplexer_3_out), .\dist (5'b01000), .out(shifter_4_out));
  Multiplexer #(.width(32)) multiplexer_4 (
    .in0(multiplexer_3_out), .in1(shifter_4_out), .out(multiplexer_4_out), .sel(A[3]));  // open: en
  Shifter #(.width(32), .shift("lr")) shifter_5 (.in(multiplexer_4_out), .\dist (5'b10000), .out(shifter_5_out));
  Multiplexer #(.width(32)) multiplexer_5 (
    .in0(multiplexer_4_out), .in1(shifter_5_out), .out(out), .sel(A[4]));  // open: en
endmodule

module sra (
  input  [31:0] B,
  input  [31:0] A,
  output [31:0] out
);

  wire [31:0] multiplexer_1_out, multiplexer_2_out, multiplexer_3_out, multiplexer_4_out, shifter_1_out,
       shifter_2_out, shifter_3_out, shifter_4_out, shifter_5_out;

  Multiplexer #(.width(32)) multiplexer_1 (
    .in0(B), .in1(shifter_1_out), .out(multiplexer_1_out), .sel(A[0]));  // open: en
  Shifter #(.width(32), .shift("ar")) shifter_1 (.in(B), .\dist (5'b00001), .out(shifter_1_out));
  Shifter #(.width(32), .shift("ar")) shifter_2 (.in(multiplexer_1_out), .\dist (5'b00010), .out(shifter_2_out));
  Multiplexer #(.width(32)) multiplexer_2 (
    .in0(multiplexer_1_out), .in1(shifter_2_out), .out(multiplexer_2_out), .sel(A[1]));  // open: en
  Shifter #(.width(32), .shift("ar")) shifter_3 (.in(multiplexer_2_out), .\dist (5'b00100), .out(shifter_3_out));
  Multiplexer #(.width(32)) multiplexer_3 (
    .in0(multiplexer_2_out), .in1(shifter_3_out), .out(multiplexer_3_out), .sel(A[2]));  // open: en
  Shifter #(.width(32), .shift("ar")) shifter_4 (.in(multiplexer_3_out), .\dist (5'b01000), .out(shifter_4_out));
  Multiplexer #(.width(32)) multiplexer_4 (
    .in0(multiplexer_3_out), .in1(shifter_4_out), .out(multiplexer_4_out), .sel(A[3]));  // open: en
  Shifter #(.width(32), .shift("ar")) shifter_5 (.in(multiplexer_4_out), .\dist (5'b10000), .out(shifter_5_out));
  Multiplexer #(.width(32)) multiplexer_5 (
    .in0(multiplexer_4_out), .in1(shifter_5_out), .out(out), .sel(A[4]));  // open: en
endmodule

module add (
  input  [31:0] X,
  input  [31:0] Y,
  output [31:0] sum,
  output cout
);

  Adder #(.width(32)) adder_1 (.a(X), .b(Y), .out(sum), .cout(cout));  // open: cin
endmodule

module addu (
  input  [31:0] X,
  input  [31:0] Y,
  output [31:0] sum
);

  Adder #(.width(32)) adder_1 (.a(X), .b(Y), .out(sum));  // open: cin, cout
endmodule

module sub (
  input  [31:0] in_1,
  input  [31:0] in_2,
  output [31:0] result,
  output cout
);

  Subtractor #(.width(32)) subtractor_1 (.a(in_1), .b(in_2), .out(result), .bout(cout));  // open: bin
endmodule

module subu (
  input  [31:0] in_1,
  input  [31:0] in_2,
  output [31:0] result
);

  Subtractor #(.width(32)) subtractor_1 (.a(in_1), .b(in_2), .out(result));  // open: bin, bout
endmodule

module \and  (
  input  [31:0] X,
  input  [31:0] Y,
  output [31:0] Output
);

  assign Output = X & Y;  // AND_Gate and_1, 32 bits wide
endmodule

module \or  (
  input  [31:0] X,
  input  [31:0] Y,
  output [31:0] Output
);

  assign Output = X | Y;  // OR_Gate or_1, 32 bits wide
endmodule

module slt__signed_comparison (
  input  [31:0] X,
  input  [31:0] Y,
  output [31:0] out
);

  Comparator #(.width(32)) comparator_1 (.a(X), .b(Y), .lt(out[0]));  // open: gt, eq

  assign out[31:1] = {31{1'b0}};
endmodule

module sltu__unsigned_comparison (
  input  [31:0] X,
  input  [31:0] Y,
  output [31:0] out
);

  Comparator #(.width(32), .mode("unsigned")) comparator_1 (.a(X), .b(Y), .lt(out[0]));  // open: gt, eq

  assign out[31:1] = {31{1'b0}};
endmodule
